// Digital circuit connection_box.dig as structural Verilog
module connection_box (
  input  in,
  input  [3:0] cfg,
  input  clk,
  output u0,
  output d0,
  output u1,
  output d1,
  output u2,
  output d2,
  output u3,
  output d3
);

  wire [3:0] d_ff_1_q;

  D_FF #(.Bits(4)) d_ff_1 (.D(cfg), .C(clk), .Q(d_ff_1_q));  // open: nQ
  NFET nfet_1 (.G(d_ff_1_q[0]), .D(in), .S(d0));
  NFET nfet_2 (.G(d_ff_1_q[1]), .D(in), .S(d1));
  NFET nfet_3 (.G(d_ff_1_q[2]), .D(in), .S(d2));
  NFET nfet_4 (.G(d_ff_1_q[3]), .D(in), .S(d3));
  // Pins of 1 and 4 bits meet at cfg

  assign u0 = d0;
  assign u1 = d1;
  assign u2 = d2;
  assign u3 = d3;
endmodule
