// Digital circuit switch_block.dig as structural Verilog
module switch_block (
  input  clk,
  input  [5:0] cfg,
  output R,
  output L,
  output U,
  output D
);

  wire s1, s2, s3, s4, s5, s6;

  Register #(.Bits(6)) register_1 (.D(cfg), .C(clk), .en(1'b1), .Q({s6, s5, s4, s3, s2, s1}));
  NFET nfet_1 (.G(s1), .D(U), .S(L));
  NFET nfet_2 (.G(s4), .D(L), .S(D));
  NFET nfet_3 (.G(s5), .D(R), .S(L));
  NFET nfet_4 (.G(s6), .D(U), .S(D));
  NFET nfet_5 (.G(s2), .D(R), .S(U));
  NFET nfet_6 (.G(s3), .D(D), .S(R));
endmodule
